// Digital circuit clk_stretching_bkp.dig as structural Verilog
module clk_stretching_bkp (
  input  clk,
  input  s_0,
  input  s_2
);

  wire and_1_out, and_2_out, and_3_out, and_4_out, and_5_out, and_6_out, and_7_out, counter_1_ovf,
       counter_2_out, counter_2_ovf, not_1_out, not_2_out, not_3_out, not_4_out, or_1_out, rs_ff_1_nq,
       rs_ff_1_q, rs_ff_2_nq, rs_ff_2_q;
  wire [2:0] counter_1_out;

  and and_1 (and_1_out, s_0, not_1_out);
  and and_2 (and_2_out, s_2, not_3_out);
  not not_1 (not_1_out, and_6_out);
  not not_2 (not_2_out, and_1_out);
  and and_3 (and_3_out, not_2_out, counter_1_ovf);
  not not_3 (not_3_out, and_7_out);
  not not_4 (not_4_out, and_2_out);
  and and_4 (and_4_out, not_4_out, counter_2_ovf);
  RS_FF rs_ff_1 (.S(and_1_out), .C(clk), .R(and_3_out), .Q(rs_ff_1_q), .nQ(rs_ff_1_nq));
  RS_FF rs_ff_2 (.S(and_2_out), .C(clk), .R(and_4_out), .Q(rs_ff_2_q), .nQ(rs_ff_2_nq));
  Counter #(.Bits(3)) counter_1 (.en(1'b1), .C(clk), .clr(rs_ff_1_nq), .out(counter_1_out), .ovf(counter_1_ovf));
  Counter counter_2 (.en(1'b1), .C(clk), .clr(rs_ff_2_nq), .out(counter_2_out), .ovf(counter_2_ovf));
  and and_5 (and_5_out, clk, rs_ff_2_nq, rs_ff_1_nq);
  and and_6 (and_6_out, counter_1_out[2], rs_ff_2_nq, rs_ff_1_q);
  or or_1 (or_1_out, and_5_out, and_6_out, and_7_out);
  and and_7 (and_7_out, counter_2_out, rs_ff_1_nq, rs_ff_2_q);
  // Probe s_clk on or_1_out
endmodule
