// Digital circuit ic_selector.dig as structural Verilog
module ic_selector (
  input  CLK,
  input  RnW,
  input  A13,
  input  A14,
  input  A15,
  output CE_RAM,
  output CE_ROM,
  output CE_KEY,
  output CE_LCD,
  output nWE,
  output nOE
);

  wire not_1_out, not_2_out, not_3_out, not_4_out;

  not not_1 (not_1_out, A15);
  not not_2 (not_2_out, A14);
  not not_3 (not_3_out, A13);
  not not_4 (not_4_out, CLK);
  and and_1 (CE_RAM, not_1_out, not_2_out, not_3_out);
  and and_2 (CE_ROM, A15, A14, A13);
  and and_3 (CE_LCD, A15, not_2_out, not_3_out);
  and and_4 (CE_KEY, A15, A14, not_3_out);
  or or_1 (nWE, RnW, not_4_out);
  nand nand_1 (nOE, RnW, CLK);

  // Notes on the sheet:
  //   RnW: default 1
endmodule
