// Digital circuit keypad_ctrl.dig as structural Verilog
module keypad_ctrl (
  input  nCE,
  input  nWE,
  input  R1,
  input  R2,
  input  R3,
  input  R4,
  input  [1:0] A,
  input  nOE,
  output C1,
  output C2,
  output C3,
  output C4,
  output [7:0] D
);

  wire nor_1_out, not_1_out;

  not not_1 (not_1_out, nWE);
  nor nor_1 (nor_1_out, nCE, nOE, not_1_out);
  Demultiplexer #(.Selector_Bits(2)) demultiplexer_1 (
    .sel(A), .in(nor_1_out), .out_0(C1), .out_1(C2), .out_2(C3), .out_3(C4));
  assign D = nor_1_out ? {4'b0000, R4, R3, R2, R1} : 8'bz;  // Driver driver_1

  // Notes on the sheet:
  //   nCE: default 1
  //   nWE: default 1
  //   A: default 1
  //   nOE: default 1
endmodule
