// Digital circuit 2b_and_gate.dig as structural Verilog
module _2b_and_gate (
  input  i_0,
  input  i_1,
  input  i_2,
  input  i_3,
  input  g,
  output o_0,
  output o_1,
  output o_2,
  output o_3
);

  and and_1 (o_0, i_0, g);
  and and_2 (o_1, i_1, g);
  and and_3 (o_2, i_2, g);
  and and_4 (o_3, i_3, g);
endmodule
