// Digital circuit gfx_p0.dig as structural Verilog
module gfx_p0 (
  input  [14:0] addr,
  input  [7:0] data,
  input  cs,
  input  we
);

  wire and_1_out;

  and and_1 (and_1_out, cs, we);
  RAMSinglePortSel #(.AddrBits(15), .Bits(8)) ramsingleportsel_1 (
    .A(addr), .CS(and_1_out), .WE(and_1_out), .OE(1'b0), .D(data));
endmodule
