// Digital circuit gfx_x2_p0.dig as structural Verilog
module gfx_x2_p0 (
  input  [15:0] addr,
  input  [7:0] data,
  input  cs,
  input  we
);

  // And and_1 has open pins: In_1=cs, In_2=we, out=open
  RAMSinglePortSel #(.AddrBits(15), .Bits(8)) ramsingleportsel_1 ();  // open: A, CS, WE, OE, D
  RAMSinglePortSel #(.AddrBits(15), .Bits(8)) ramsingleportsel_2 ();  // open: A, CS, WE, OE, D
endmodule
