// Digital circuit spriteRenderer.dig as structural Verilog
module spriteRenderer (
  input  clk,
  input  [8:0] line_y,
  output [7:0] out_2,
  output [7:0] out_3,
  output [7:0] out_5,
  output [7:0] out_6,
  output [7:0] out_7,
  output out_8,
  output [7:0] out_9,
  output [8:0] out_10,
  output [8:0] out_11,
  output [14:0] out_12,
  output [2:0] out_13,
  output [3:0] out_14,
  output [2:0] out_15,
  output [3:0] out_16,
  output [14:0] out_17,
  output [7:0] out_18,
  output [9:0] out_19,
  output [8:0] out_20,
  output out_21,
  output [5:0] out_22
);

  wire decoder_1_out_0, decoder_1_out_1, decoder_1_out_2, decoder_1_out_3, not_1_out, not_2_out, or_1_out,
       replace_with_nand_2_eq, rs_0, rs_1, rs_2, rs_3, rs_pload, s_preload;

  Counter #(.Bits(4)) counter_1 (.en(1'b1), .C(clk), .clr(out_21), .out(out_16));  // open: ovf
  Decoder #(.Selector_Bits(2)) decoder_1 (
    .sel(out_16[1:0]), .out_0(decoder_1_out_0), .out_1(decoder_1_out_1), .out_2(decoder_1_out_2),
    .out_3(decoder_1_out_3));
  nor nor_1 (rs_pload, out_16[2], out_16[3]);
  Sub #(.Bits(4)) sub_1 (.a(out_16), .b(4'b0100), .c_i(1'b0), .s({out_14[3], out_12[2:0]}));  // open: c_o
  Comparator #(.Bits(4)) replace_with_nand (.a(out_16), .b(4'b1100), .eq(out_21));  // open: gt, lt
  _2b_and_gate _2b_and_gate_1 (
    .i_0(decoder_1_out_0), .i_1(decoder_1_out_1), .i_2(decoder_1_out_2), .i_3(decoder_1_out_3), .g(rs_pload),
    .o_0(rs_0), .o_1(rs_1), .o_2(rs_2), .o_3(rs_3));
  or or_1 (or_1_out, rs_3, rs_2, rs_1, rs_0);
  and and_1 (s_preload, rs_pload, or_1_out);
  Counter #(.Bits(6)) counter_2 (.en(1'b1), .C(out_21), .clr(1'b0), .out(out_22));  // open: ovf
  Multiplexer #(.Bits(15)) multiplexer_1 (
    .sel(s_preload), .in_0({out_6[6], out_5, out_7[2:0], out_12[2:0]}),
    .in_1({{7{1'b0}}, out_22, out_16[1:0]}), .out(out_17));
  Register #(.Bits(8)) register_1 (.D(out_18), .C(clk), .en(rs_0), .Q(out_2));
  Register #(.Bits(8)) register_2 (.D(out_18), .C(clk), .en(rs_1), .Q(out_3));
  Register #(.Bits(8)) register_3 (.D(out_18), .C(clk), .en(rs_2), .Q(out_5));
  Register #(.Bits(8)) register_4 (.D(out_18), .C(clk), .en(rs_3), .Q(out_6));
  ROM #(.AddrBits(15), .Bits(8)) rom_1 (.A(out_17), .sel(1'b1), .D(out_18));
  Sub #(.Bits(8)) sub_2 (.a(line_y[8:1]), .b(out_2), .c_i(1'b0), .s(out_7), .c_o(out_8));
  Add #(.Bits(9)) add_1 (
    .a({{6{1'b0}}, out_12[2:0]}), .b({out_6[7], out_3}), .c_i(1'b0), .s(out_19[8:0]));  // open: c_o
  Comparator #(.Bits(8)) replace_with_nand_2 (.a(out_18), .b({8{1'b0}}), .eq(replace_with_nand_2_eq));  // open: gt, lt
  not not_1 (not_1_out, replace_with_nand_2_eq);
  not not_2 (not_2_out, rs_pload);
  RAMSinglePortSel #(.AddrBits(10), .Bits(8)) RENDER_MEM (
    .A({1'b0, out_19[8:0]}), .CS(not_2_out), .WE(not_1_out), .OE(1'b0), .D(out_18));

  assign out_9 = line_y[8:1];
  assign out_10 = {out_6[6], out_5};
  assign out_11 = {out_6[7], out_3};
  assign out_12[14:3] = {out_6[6], out_5, out_7[2:0]};
  assign out_13 = out_7[2:0];
  assign out_14[2:0] = out_12[2:0];
  assign out_15 = out_12[2:0];
  assign out_19[9] = 1'b0;
  assign out_20 = out_19[8:0];

  // Other names for the same wires on the sheet: line_p = line_y[0]; line_n[7:0] = line_y[8:1];
  //   s_x[8:0] = {out_6[7], out_3}; s_i[8:0] = {out_6[6], out_5}; s_yd[2:0] = out_7[2:0]; rp_addr[2:0] = out_12[2:0];
  //   rs_addr[1:0] = out_16[1:0]; rom_d[7:0] = out_18; rs_end = out_21; s_c[7:0] = out_6; s_i9 = out_6[6];
  //   s_x9 = out_6[7]; s_y[7:0] = out_2

  // Notes on the sheet:
  //   line_y: default 28
  //   contents of rom_1 (hex, n*v repeats v):
  //   a,bb,cc,dd,29468*0,a,0,1e,28,32,3c,b,c8
endmodule
