// Digital circuit test.dig as structural Verilog
module test (
  input  clk,
  input  clk_2,
  input  set,
  output [3:0] out_4
);

  wire counter_1_ovf, or_1_out, or_2_out, register_1_q;

  or or_1 (or_1_out, clk_2, clk);
  or or_2 (or_2_out, set, ~counter_1_ovf);  // Or
  Register register_1 (.D(or_2_out), .C(or_1_out), .en(1'b1), .Q(register_1_q));
  Counter #(.Bits(4)) counter_1 (.en(register_1_q), .C(clk_2), .clr(1'b0), .out(out_4), .ovf(counter_1_ovf));

  // Other names for the same wires on the sheet: clk_0 = clk; clk_1 = clk_2

  // Notes on the sheet:
  //   clk_2: Hz: 3
endmodule
