// Digital circuit video_circ.dig as structural Verilog
module video_circ (
  input  clk,
  output [9:0] H_CNT,
  output H_SYNC,
  output V_SYNC,
  output [9:0] V_CNT,
  output [7:0] out_6,
  output [7:0] out_7,
  output [3:0] out_8
);

  wire comparator_1_eq, comparator_2_eq, comparator_3_lt, comparator_4_gt, comparator_5_lt, comparator_6_gt;

  Counter #(.Bits(10)) counter_1 (.en(1'b1), .C(clk), .clr(comparator_1_eq), .out(H_CNT));  // open: ovf
  Counter #(.Bits(10)) counter_2 (.en(1'b1), .C(comparator_1_eq), .clr(comparator_2_eq), .out(V_CNT));  // open: ovf
  Comparator #(.Bits(10)) comparator_1 (.a(H_CNT), .b(10'h320), .eq(comparator_1_eq));  // open: gt, lt
  Comparator #(.Bits(10)) comparator_2 (.a(V_CNT), .b(10'h20d), .eq(comparator_2_eq));  // open: gt, lt
  EEPROM #(.AddrBits(17), .Bits(8)) eeprom_1 (.A({V_CNT[8:0], H_CNT[8:1]}), .CS(1'b1), .WE(1'b0), .OE(1'b1), .D(out_6));
  Comparator #(.Bits(10)) comparator_3 (.a(H_CNT), .b(10'h290), .lt(comparator_3_lt));  // open: gt, eq
  Comparator #(.Bits(10)) comparator_4 (.a(H_CNT), .b(10'h2ef), .gt(comparator_4_gt));  // open: eq, lt
  Comparator #(.Bits(10)) comparator_5 (.a(V_CNT), .b(10'h1ea), .lt(comparator_5_lt));  // open: gt, eq
  Comparator #(.Bits(10)) comparator_6 (.a(V_CNT), .b(10'h1eb), .gt(comparator_6_gt));  // open: eq, lt
  Register #(.Bits(8)) register_1 (.D(out_6), .C(clk), .en(H_CNT[0]), .Q(out_7));
  or or_1 (H_SYNC, comparator_3_lt, comparator_4_gt);
  or or_2 (V_SYNC, comparator_5_lt, comparator_6_gt);
  Multiplexer #(.Bits(4)) multiplexer_1 (.sel(H_CNT[0]), .in_0(out_7[3:0]), .in_1(out_7[7:4]), .out(out_8));

  // Notes on the sheet:
  //   clk: Hz: 2
  //   752 - 1
  //   492 - 1
  //   contents of eeprom_1 (hex, n*v repeats v):
  //   11,12,13,14,15,16,17,18,19,1a,1b,1c,1d,1e,1f,11,21,12,13,14,15
  //   ,16,17,18,19,1a,1b,1c,1d,1e,1f,11
endmodule
