// Digital circuit sprite_render.dig as structural Verilog
module sprite_render (
  input  v_clk
);

  wire not_1_out, sprite_line_renderer_1_oe_s, sprite_line_renderer_1_we_r, vga_sig_1_nd_out,
       vga_sig_1_nh_sync, vga_sig_1_nv_sync;
  wire [0:0] vga_sig_1_h_cnt;
  wire [7:0] dp_ram_1_d_r, ramsingleportsel_1_d;
  wire [9:0] sprite_line_renderer_1_a_r, vga_sig_1_h_cnt_2, vga_sig_1_v_cnt;
  wire [14:0] sprite_line_renderer_1_a_s;

  not not_1 (not_1_out, sprite_line_renderer_1_we_r);
  dp_ram dp_ram_1 (
    .nCE_L(1'b0), .RnW_L(not_1_out), .nOE_L(1'b1), .A_L(sprite_line_renderer_1_a_r),
    .D_L(ramsingleportsel_1_d), .nCE_R(1'b1), .RnW_R(1'b1), .nOE_R(vga_sig_1_nd_out),
    .A_R(vga_sig_1_h_cnt_2), .D_R(dp_ram_1_d_r));
  vga_sig vga_sig_1 (
    .clk(v_clk), .nh_sync(vga_sig_1_nh_sync), .nv_sync(vga_sig_1_nv_sync), .nd_out(vga_sig_1_nd_out),
    .h_cnt({vga_sig_1_h_cnt_2[8:0], vga_sig_1_h_cnt[0]}),
    .v_cnt({vga_sig_1_v_cnt[9:2], vga_sig_1_h_cnt_2[9], vga_sig_1_v_cnt[0]}));  // open: d_out
  RAMSinglePortSel #(.AddrBits(15), .Bits(8)) ramsingleportsel_1 (
    .A(sprite_line_renderer_1_a_s), .CS(1'b1), .WE(1'b0), .OE(sprite_line_renderer_1_oe_s),
    .D(ramsingleportsel_1_d));
  vga_port vga_port_1 (.RGB(dp_ram_1_d_r[2:0]), .nH_SYNC(vga_sig_1_nh_sync), .nV_SYNC(vga_sig_1_nv_sync));
  sprite_line_renderer sprite_line_renderer_1 (
    .clk(vga_sig_1_h_cnt[0]), .A_s(sprite_line_renderer_1_a_s), .D_s(ramsingleportsel_1_d),
    .OE_s(sprite_line_renderer_1_oe_s),
    .n_line({vga_sig_1_v_cnt[8:2], vga_sig_1_h_cnt_2[9], vga_sig_1_v_cnt[0]}),
    .WE_r(sprite_line_renderer_1_we_r), .A_r(sprite_line_renderer_1_a_r));
endmodule
