// Digital circuit wavegenerator.dig as structural Verilog
module wavegenerator (
  input  W,
  input  EN,
  input  [7:0] DATA,
  input  A0,
  input  CLK,
  input  RN,
  output [11:0] out_7,
  output [11:0] out_8
);

  wire and_1_out, and_2_out, and_3_out, CLK2, not_1_out, not_2_out, not_3_out;

  not not_1 (not_1_out, EN);
  not not_2 (not_2_out, A0);
  not not_3 (not_3_out, EN);
  Counter #(.Bits(9)) counter_1 (.en(EN), .C(CLK2), .clr(not_1_out));  // open: out, ovf
  and and_1 (and_1_out, EN, RN);
  and and_2 (and_2_out, W, EN, not_2_out);
  and and_3 (and_3_out, A0, EN, W);
  Register #(.Bits(8)) register_1 (.D(DATA), .C(CLK), .en(and_2_out), .Q(out_7[7:0]));
  Register #(.Bits(4)) register_2 (.D(DATA[3:0]), .C(CLK), .en(and_3_out), .Q(out_7[11:8]));
  Counter #(.Bits(12)) counter_2 (.en(and_1_out), .C(CLK), .clr(not_3_out), .out(out_8));  // open: ovf
  Comparator #(.Bits(12)) comparator_1 (.a(out_7), .b(out_8), .gt(CLK2));  // open: eq, lt
endmodule
